# Fritzing sketch PowerboostOnOffStrip (saved by Fritzing 0.9.3b)
stripboards: 1

parts:
  part = Pushbutton [package="[THT]"]
  part_2 = Rectifier Diode [part_number=1N4001 package="Melf DO-213 AB [SMD]"]
  part_3 = Resistor [tolerance=±5% resistance=100k package=THT]
  part_4 = Resistor [tolerance=±5% resistance=33k package=THT]
  part_5 = Resistor [tolerance=±5% resistance=10k package=THT]
  part_6 = Resistor [tolerance=±5% resistance=100k package=THT]
  100uF = Capacitor Polarized [package=cpol-radial-100uf-25v]
  Part2 = Adafruit Stereo 3W Speaker Bonnet [part_number="Adafruit #"]
  Part4 = PowerBoost 1000 Basic

nets:
  N1: part.Pin_1, part_2.anode, part_4.Pin_1
  N2: part.Pin_3, Part4.VBAT
  N3: part_2.cathode, part_5.Pin_1, part_6.Pin_0, 100uF.+, Part4.ENABLE
  GND: part_3.Pin_0, part_6.Pin_1, 100uF.-, Part2.GND, Part4.GND
  N4: part_3.Pin_1, part_4.Pin_0, Part2.GPIO27
  N5: part_5.Pin_0, Part2.TXD
  N6: Part2.RXD, Part4.LBO
  N7: Part2.5.0V, Part4.5.0V

notes:
  power button

custom parts:
  Adafruit Stereo 3W Speaker Bonnet: Hey Mr. DJ! Turn up that Raspberry Pi mix to the max with this cute 3W Stereo Amplifier Bonnet for Raspberry Pi. (It's not big enough to be an official HAT, so we called it a bonnet, you see?) It's the exact same size as a Raspberry Pi Zero but works with any and all Raspberry Pi computers with a 2x20 connector - A+, B+, Zero, Pi 2, Pi 3, etc. This Bonnet uses I2S a digital sound standard, so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
  PowerBoost 1000 Basic: The PowerBoost 1000 is a little DC/DC boost converter module that can run from 1.8V batteries or higher, and convert the battery output to 5.2V DC for running your 5V projects. At its heart is a TPS61030 boost converter from TI. This boost converter chip has some really nice extras such as low battery detection, 4A internal switch, synchronous conversion, excellent efficiency, and 700KHz high-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
